# Fritzing sketch FSR+MCP3008 (saved by Fritzing 0.9.3b)
breadboards: 1

parts:
  IC1 = MCP3008 8-channel 10-bit ADC [part_number=MCP3008]
  Raspberry_Pi1 = Raspberry Pi 2
  J1 = Basic Force Sensing Resistor (FSR) [package=THT]
  R1 = Resistor [tolerance=±5% resistance=10k package="0603 [SMD]"]

nets:
  N1: IC1.no_name_yet#1, J1.pin_1, R1.Pin_0
  N2: IC1.no_name_yet#9, Raspberry_Pi1.GPIO17, R1.Pin_1
  N3: IC1.no_name_yet#10, Raspberry_Pi1.GPIO8
  N4: IC1.no_name_yet#11, Raspberry_Pi1.GPIO10
  N5: IC1.no_name_yet#12, Raspberry_Pi1.GPIO9
  N6: IC1.no_name_yet#13, Raspberry_Pi1.GPIO11
  N7: IC1.no_name_yet#14, Raspberry_Pi1.GPIO14
  3V3: IC1.no_name_yet#15, IC1.no_name_yet#16, Raspberry_Pi1.3v3, Raspberry_Pi1.3V3, J1.pin_0
