# Fritzing sketch LED+ShiftRegister(74HC595) (saved by Fritzing 0.9.3b)
breadboards: 1

parts:
  U1 = 74HC595 SMD [package="SO16 [SMD]"]
  LED1 = smd LED [color="Red (633nm)" package="1206 [SMD]"]
  Part1 = Arduino Nano (Rev3.0)
  LED2 = smd LED [color="Red (633nm)" package="1206 [SMD]"]
  LED3 = smd LED [color="Red (633nm)" package="1206 [SMD]"]
  LED4 = smd LED [color="Red (633nm)" package="1206 [SMD]"]
  LED5 = smd LED [color="Red (633nm)" package="1206 [SMD]"]
  LED6 = smd LED [color="Red (633nm)" package="1206 [SMD]"]
  LED7 = smd LED [color="Red (633nm)" package="1206 [SMD]"]
  LED8 = smd LED [color="Red (633nm)" package="1206 [SMD]"]

nets:
  N1: U1.Q1, LED2.anode
  N2: U1.Q2, LED3.anode
  N3: U1.Q3, LED4.anode
  N4: U1.Q4, LED8.anode
  N5: U1.Q5, LED5.anode
  N6: U1.Q6, LED7.anode
  N7: U1.Q7, LED6.anode
  GND: U1.GND, U1.OE, LED1.cathode, Part1.GND, LED2.cathode, LED3.cathode, LED4.cathode, LED5.cathode, LED6.cathode, LED7.cathode, LED8.cathode
  VCC: U1.MR, U1.VCC, Part1.5V
  N8: U1.SH_CP, Part1.D6
  N9: U1.ST_CP, Part1.D5
  N10: U1.DS, Part1.D4
  N11: U1.Q0, LED1.anode
