# Fritzing sketch MCP23017_LCD (saved by Fritzing 0.9.2b)
breadboards: 1

parts:
  Raspberry_Pi1 = Raspberry Pi 2
  IC1 = MCP23017 I2C I/O Expander
  LCD1 = LCD screen

nets:
  3V3: Raspberry_Pi1.3v3, IC1.VDD
  N1: Raspberry_Pi1.GPIO2, IC1.SDA
  N2: Raspberry_Pi1.GPIO3, IC1.SCL
  VSS: Raspberry_Pi1.GND, IC1.VSS, LCD1.VSS, LCD1.V0, LCD1.R/W, LCD1.LED-
  5V: Raspberry_Pi1.5V, LCD1.VDD, LCD1.LED+
  N3: IC1.GPB0, LCD1.DB4
  N4: IC1.GPB1, LCD1.DB5
  N5: IC1.GPB2, LCD1.DB6
  N6: IC1.GPB3, LCD1.DB7
  N7: IC1.GPB4, LCD1.E
  N8: IC1.GPB6, LCD1.RS

notes:
  Pin 15 of the LCD can be connected to GPB7 on MCP23017 - Pin15 (Adafruit library) if wish to control backlight.

custom parts:
  MCP23017 I2C I/O Expander: The MCP23017 uses two i2c pins (these can be shared with other i2c devices), and in exchange gives you 16 general purpose pins. You can set each of 16 pins to be input, output, input with a pullup or open drain. There's even the ability to get an interrupt via an external pin when any of the inputs change so you don't have to keep polling the chip.
