# Fritzing sketch MCP3008_LM35 (saved by Fritzing 0.9.2b)
breadboards: 1

parts:
  Raspberry_Pi1 = Raspberry Pi 2
  IC1 = MCP3008 8-channel 10-bit ADC [part_number=MCP3008]
  T1 = LM35 Temperature Sensor [package="TO92 [THT]"]

nets:
  3V3: Raspberry_Pi1.3v3, Raspberry_Pi1.3V3, IC1.no_name_yet#15, IC1.no_name_yet#16
  N1: Raspberry_Pi1.GPIO10, IC1.no_name_yet#11
  N2: Raspberry_Pi1.GPIO9, IC1.no_name_yet#12
  N3: Raspberry_Pi1.GPIO11, IC1.no_name_yet#13
  N4: Raspberry_Pi1.GPIO8, IC1.no_name_yet#10
  GND: Raspberry_Pi1.GND, IC1.no_name_yet#9, IC1.no_name_yet#14, T1.GND
  N5: Raspberry_Pi1.5V, T1.+Vs
  N6: IC1.no_name_yet#1, T1.Vout
